// Logisim project trabalho-cafe.circ as structural Verilog: 8 circuits, main circuit contador de 3 bits
module contador_de_3_bits (
  input  EntCnt,
  input  Reset,
  output Q0,
  output Q1,
  output Q2
);

  wire and_1_out, and_2_out;

  and and_1 (and_1_out, 1'b1, Q0);
  J_K_Flip_Flop j_k_ff_1 (.J(1'b1), .clk(EntCnt), .K(1'b1), .Q(Q0), .reset(Reset));  // open: Qn, preset, en
  J_K_Flip_Flop j_k_ff_2 (.J(and_1_out), .clk(EntCnt), .K(and_1_out), .Q(Q1), .reset(Reset));  // open: Qn, preset, en
  and and_2 (and_2_out, and_1_out, Q1);
  J_K_Flip_Flop j_k_ff_3 (.J(and_2_out), .clk(EntCnt), .K(and_2_out), .Q(Q2), .reset(Reset));  // open: Qn, preset, en
  // AND_Gate and_3 has open pins: in0=and_2_out, in1=Q2, out=open
endmodule

module BCD_7segmentos (
  input  BCD0,
  input  BCD1,
  input  BCD2,
  input  BCD3,
  output a,
  output b,
  output c,
  output d,
  output e,
  output f,
  output g
);

  wire and_1_out, and_2_out, and_3_out, and_4_out, and_5_out, and_6_out, and_7_out, and_8_out, and_9_out,
       and_10_out, and_11_out, and_12_out, and_13_out, and_14_out, and_15_out, and_16_out, and_17_out,
       and_18_out, and_19_out, and_20_out, and_21_out, not_1_out, not_2_out, not_3_out, not_4_out, not_5_out,
       not_6_out, not_7_out, not_8_out, not_9_out, not_10_out, not_11_out, not_12_out, not_13_out,
       not_14_out, not_15_out, not_16_out, not_17_out, not_18_out, not_19_out, not_20_out, not_21_out,
       not_22_out, not_23_out, not_24_out, not_25_out, not_26_out, not_27_out, not_28_out, not_29_out,
       not_30_out, not_31_out, not_32_out, not_33_out, not_34_out, not_35_out, not_36_out, not_37_out,
       not_38_out;

  not not_1 (not_1_out, BCD1);
  and and_1 (and_1_out, not_1_out, not_2_out);
  not not_2 (not_2_out, BCD3);
  and and_2 (and_2_out, BCD1, BCD3);
  not not_3 (not_3_out, BCD1);
  not not_4 (not_4_out, BCD2);
  and and_3 (and_3_out, not_4_out, not_5_out);
  not not_5 (not_5_out, BCD3);
  and and_4 (and_4_out, BCD2, BCD3);
  not not_6 (not_6_out, BCD1);
  and and_5 (and_5_out, not_6_out, not_7_out);
  not not_7 (not_7_out, BCD2);
  not not_8 (not_8_out, BCD0);
  and and_6 (and_6_out, not_8_out, BCD3);
  not not_9 (not_9_out, BCD0);
  and and_7 (and_7_out, not_9_out, BCD1);
  not not_10 (not_10_out, BCD1);
  and and_8 (and_8_out, not_10_out, not_11_out);
  not not_11 (not_11_out, BCD3);
  not not_12 (not_12_out, BCD1);
  and and_9 (and_9_out, not_12_out, BCD2);
  and and_10 (and_10_out, BCD2, not_13_out);
  not not_13 (not_13_out, BCD3);
  and and_11 (and_11_out, BCD1, not_14_out, BCD3);
  not not_14 (not_14_out, BCD2);
  not not_15 (not_15_out, BCD1);
  and and_12 (and_12_out, not_15_out, not_16_out);
  not not_16 (not_16_out, BCD3);
  and and_13 (and_13_out, BCD2, not_17_out);
  not not_17 (not_17_out, BCD3);
  and and_14 (and_14_out, BCD0, BCD2);
  and and_15 (and_15_out, BCD0, BCD1);
  not not_18 (not_18_out, BCD0);
  not not_19 (not_19_out, BCD2);
  not not_20 (not_20_out, BCD3);
  not not_21 (not_21_out, BCD2);
  not not_22 (not_22_out, not_23_out);
  not not_23 (not_23_out, BCD1);
  not not_24 (not_24_out, BCD1);
  not not_25 (not_25_out, not_24_out);
  not not_26 (not_26_out, BCD3);
  not not_27 (not_27_out, BCD0);
  not not_28 (not_28_out, not_29_out);
  not not_29 (not_29_out, BCD1);
  not not_30 (not_30_out, BCD2);
  not not_31 (not_31_out, BCD1);
  not not_32 (not_32_out, BCD2);
  not not_33 (not_33_out, not_32_out);
  not not_34 (not_34_out, BCD2);
  not not_35 (not_35_out, not_34_out);
  not not_36 (not_36_out, BCD3);
  or or_1 (a, and_1_out, BCD2, and_2_out, BCD0);
  or or_2 (b, not_3_out, and_3_out, and_4_out, BCD0);
  or or_3 (c, and_5_out, and_6_out, and_7_out);
  or or_4 (d, and_8_out, and_9_out, and_10_out, and_11_out, BCD0);
  or or_5 (e, and_12_out, and_13_out, and_14_out, and_15_out);
  not not_37 (not_37_out, not_18_out);
  and and_16 (and_16_out, not_19_out, not_20_out);
  and and_17 (and_17_out, not_21_out, not_22_out);
  and and_18 (and_18_out, not_25_out, not_26_out);
  not not_38 (not_38_out, not_27_out);
  and and_19 (and_19_out, not_28_out, not_30_out);
  and and_20 (and_20_out, not_31_out, not_33_out);
  and and_21 (and_21_out, not_35_out, not_36_out);
  or or_6 (f, not_37_out, and_16_out, and_17_out, and_18_out);
  or or_7 (g, not_38_out, and_19_out, and_20_out, and_21_out);
endmodule

module Contador_de_2bits (
  input  EntCnt,
  input  Reset,
  output Q0,
  output Q1
);

  wire and_1_out;

  and and_1 (and_1_out, 1'b1, Q0);
  J_K_Flip_Flop j_k_ff_1 (.J(1'b1), .clk(EntCnt), .K(1'b1), .Q(Q0), .reset(Reset));  // open: Qn, preset, en
  J_K_Flip_Flop j_k_ff_2 (.J(and_1_out), .clk(EntCnt), .K(and_1_out), .Q(Q1), .reset(Reset));  // open: Qn, preset, en
  // AND_Gate and_2 has open pins: in0=and_1_out, in1=Q1, out=open
endmodule

module \Máquina_bebida  (
  input  Moeda_de_10_cents,
  input  Moeda_de_20_cents,
  input  \Café ,
  input  Chocolate,
  output \Café_2 ,
  output Chocolate_2,
  output devolvidas
);

  wire bcd_7segmentos_1_a, bcd_7segmentos_1_b, bcd_7segmentos_1_c, bcd_7segmentos_1_d, bcd_7segmentos_1_e,
       bcd_7segmentos_1_f, bcd_7segmentos_1_g, comparador_de_3_bits_1_a___b, comparador_de_3_bits_2_a___b,
       contador_de_2bits_1_q0, contador_de_2bits_1_q1, contador_de_3_bits_1_q0, contador_de_3_bits_1_q1,
       contador_de_3_bits_1_q2, d_ff_1_q, d_ff_2_q, not_1_out, not_2_out, somador_3_bits_1_c0,
       somador_3_bits_1_c1, somador_3_bits_1_c2, xor_1_out;

  contador_de_3_bits contador_de_3_bits_1 (
    .EntCnt(Moeda_de_10_cents), .Q0(contador_de_3_bits_1_q0), .Q1(contador_de_3_bits_1_q1),
    .Q2(contador_de_3_bits_1_q2), .Reset(xor_1_out));
  Contador_de_2bits contador_de_2bits_1 (
    .EntCnt(Moeda_de_20_cents), .Q0(contador_de_2bits_1_q0), .Q1(contador_de_2bits_1_q1), .Reset(xor_1_out));
  ExactlyOne xor_1 (.out(xor_1_out), .in0(devolvidas), .in1(d_ff_2_q), .in2(d_ff_1_q));
  somador_3_bits somador_3_bits_1 (
    .A2(contador_de_3_bits_1_q2), .A1(contador_de_3_bits_1_q1), .A0(contador_de_3_bits_1_q0),
    .B2(contador_de_2bits_1_q1), .B1(contador_de_2bits_1_q0), .B0(1'b0), .C2(somador_3_bits_1_c2),
    .C1(somador_3_bits_1_c1), .C0(somador_3_bits_1_c0));
  not not_1 (not_1_out, \Café );
  D_Flip_Flop d_ff_1 (.clk(not_1_out), .D(\Café_2 ), .Q(d_ff_1_q), .reset(d_ff_1_q));  // open: Qn, preset, en
  not not_2 (not_2_out, Chocolate);
  D_Flip_Flop d_ff_2 (.clk(not_2_out), .D(Chocolate_2), .Q(d_ff_2_q), .reset(d_ff_2_q));  // open: Qn, preset, en
  BCD_7segmentos bcd_7segmentos_1 (
    .BCD0(1'b0), .BCD1(somador_3_bits_1_c2), .BCD2(somador_3_bits_1_c1), .BCD3(somador_3_bits_1_c0),
    .a(bcd_7segmentos_1_a), .b(bcd_7segmentos_1_b), .c(bcd_7segmentos_1_c), .d(bcd_7segmentos_1_d),
    .e(bcd_7segmentos_1_e), .f(bcd_7segmentos_1_f), .g(bcd_7segmentos_1_g));
  _7_Segment_Display u_7_segment_display_1 (
    .g(bcd_7segmentos_1_g), .f(bcd_7segmentos_1_f), .a(bcd_7segmentos_1_a), .b(bcd_7segmentos_1_b),
    .e(bcd_7segmentos_1_e), .d(bcd_7segmentos_1_d), .c(bcd_7segmentos_1_c));  // open: dp
  comparador_de_3_bits comparador_de_3_bits_1 (
    .A2(somador_3_bits_1_c2), .A1(somador_3_bits_1_c1), .A0(somador_3_bits_1_c0), .B2(1'b0), .B1(1'b1),
    .B0(1'b1), .Enable(\Café ), .A___B(comparador_de_3_bits_1_a___b), .A___B_2(\Café_2 ));  // open: B___A
  comparador_de_3_bits comparador_de_3_bits_2 (
    .A2(somador_3_bits_1_c2), .A1(somador_3_bits_1_c1), .A0(somador_3_bits_1_c0), .B2(1'b1), .B1(1'b0),
    .B0(1'b0), .Enable(Chocolate), .A___B(comparador_de_3_bits_2_a___b), .A___B_2(Chocolate_2));  // open: B___A
  or or_1 (devolvidas, comparador_de_3_bits_2_a___b, comparador_de_3_bits_1_a___b);
endmodule

module somador_3_bits (
  input  A2,
  input  A1,
  input  A0,
  input  B2,
  input  B1,
  input  B0,
  output C2,
  output C1,
  output C0
);

  wire adder_2_cout, adder_3_cout;

  Adder #(.width(1)) adder_1 (.a(A2), .b(B2), .out(C2), .cin(adder_2_cout));  // open: cout
  Adder #(.width(1)) adder_2 (.a(A1), .b(B1), .out(C1), .cin(adder_3_cout), .cout(adder_2_cout));
  Adder #(.width(1)) adder_3 (.a(A0), .b(B0), .out(C0), .cout(adder_3_cout));  // open: cin

  // Notes on the sheet:
  //   +
  //   =
endmodule

module comparador_de_3_bits (
  input  A2,
  input  A1,
  input  A0,
  input  B2,
  input  B1,
  input  B0,
  input  Enable,
  output A___B,
  output A___B_2,
  output B___A
);

  wire comparador_de_2_bits_1_x, comparador_de_2_bits_1_y, comparador_de_2_bits_2_x,
       comparador_de_2_bits_2_y, comparador_de_2_bits_3_x, comparador_de_2_bits_3_y, nor_1_out;

  comparador_de_2_bits comparador_de_2_bits_1 (
    .AX(A2), .BY(B2), .Xn1(1'b0), .Yn1(1'b0), .X(comparador_de_2_bits_1_x), .Y(comparador_de_2_bits_1_y));
  comparador_de_2_bits comparador_de_2_bits_2 (
    .AX(A1), .BY(B1), .Xn1(comparador_de_2_bits_1_x), .Yn1(comparador_de_2_bits_1_y),
    .X(comparador_de_2_bits_2_x), .Y(comparador_de_2_bits_2_y));
  comparador_de_2_bits comparador_de_2_bits_3 (
    .AX(A0), .BY(B0), .Xn1(comparador_de_2_bits_2_x), .Yn1(comparador_de_2_bits_2_y),
    .X(comparador_de_2_bits_3_x), .Y(comparador_de_2_bits_3_y));
  nor nor_1 (nor_1_out, comparador_de_2_bits_3_x, comparador_de_2_bits_3_y);
  Multiplexer multiplexer_1 (.in0(1'b0), .in1(nor_1_out), .out(A___B_2), .sel(Enable));
  Multiplexer multiplexer_2 (.in0(1'b0), .in1(comparador_de_2_bits_3_x), .out(A___B), .sel(Enable));
  Multiplexer multiplexer_3 (.in0(1'b0), .in1(comparador_de_2_bits_3_y), .out(B___A), .sel(Enable));
endmodule

module comparador_de_2_bits (
  input  AX,
  input  BY,
  input  Xn1,
  input  Yn1,
  output X,
  output Y
);

  wire and_1_out, and_2_out, not_1_out, not_2_out, not_3_out, not_4_out;

  not not_1 (not_1_out, BY);
  and and_1 (and_1_out, AX, not_1_out, not_2_out);
  not not_2 (not_2_out, Yn1);
  not not_3 (not_3_out, AX);
  and and_2 (and_2_out, not_3_out, not_4_out, BY);
  not not_4 (not_4_out, Xn1);
  or or_1 (X, and_1_out, Xn1);
  or or_2 (Y, and_2_out, Yn1);
endmodule

module \implementação  (
  input  Cafe,
  input  Chocolate,
  output \Café ,
  output Chocolate_2,
  output Retirar_bebida
);

  wire d_ff_1_q, d_ff_1_qn, d_ff_2_q, d_ff_2_qn, d_ff_3_q, d_ff_4_q, Moeda_de_10_cents_out,
       Moeda_de_20_cents_out;

  Clock Moeda_de_10_cents (.out(Moeda_de_10_cents_out));
  Clock Moeda_de_20_cents (.out(Moeda_de_20_cents_out));
  D_Flip_Flop d_ff_1 (
    .clk(Moeda_de_10_cents_out), .D(d_ff_1_qn), .Q(d_ff_1_q), .Qn(d_ff_1_qn));  // open: preset, en, reset
  D_Flip_Flop d_ff_2 (
    .clk(Moeda_de_20_cents_out), .D(d_ff_2_qn), .Q(d_ff_2_q), .Qn(d_ff_2_qn));  // open: preset, en, reset
  D_Flip_Flop d_ff_3 (.clk(Cafe), .D(Cafe), .Q(d_ff_3_q), .reset(\Café ));  // open: Qn, preset, en
  \Máquina_bebida  \máquina_bebida_1  (
    .Moeda_de_10_cents(d_ff_1_q), .Moeda_de_20_cents(d_ff_2_q), .\Café (d_ff_3_q), .Chocolate(d_ff_4_q),
    .\Café_2 (\Café ), .Chocolate_2(Chocolate_2), .devolvidas(Retirar_bebida));
  D_Flip_Flop d_ff_4 (.clk(Chocolate), .D(Chocolate), .Q(d_ff_4_q), .reset(Chocolate_2));  // open: Qn, preset, en
endmodule
